# Fritzing sketch AR14_4LED (saved by Fritzing 0.9.3b)
breadboards: 1

parts:
  부품1 = Arduino Uno (Rev3)
  LED1 = LED - 5mm [color="Yellow (595nm)" package="5 mm [THT]"]
  R1 = Resistor [tolerance=±5% resistance=335 package=THT]
  R2 = Resistor [tolerance=±5% resistance=335 package=THT]
  R3 = Resistor [tolerance=±5% resistance=335 package=THT]
  R4 = Resistor [tolerance=±5% resistance=335 package=THT]
  LED2 = LED - 5mm [color="Blue (470nm)" package="5 mm [THT]"]
  LED3 = LED - 5mm [color="Green (570nm)" package="5 mm [THT]"]
  LED4 = LED - 5mm [color="Red (633nm)" package="5 mm [THT]"]

nets:
  N1: 부품1.D9_PWM, LED1.cathode
  N2: 부품1.D3_PWM, LED4.cathode
  N3: 부품1.D5_PWM, LED3.cathode
  N4: 부품1.D6_PWM, LED2.cathode
  N5: 부품1.GND, R1.Pin_1, R2.Pin_1, R3.Pin_1, R4.Pin_1
  N6: LED1.anode, R1.Pin_0
  N7: R2.Pin_0, LED2.anode
  N8: R3.Pin_0, LED3.anode
  N9: R4.Pin_0, LED4.anode
