# Fritzing sketch AR14_RGB (saved by Fritzing 0.9.3b)
breadboards: 1

parts:
  부품1 = Arduino Uno (Rev3)
  LED1 = Super Flux RGB LED (com. anode)

nets:
  N1: 부품1.D3_PWM, LED1.red_cathode
  N2: 부품1.D5_PWM, LED1.green_cathode
  N3: 부품1.D6_PWM, LED1.blue_cathode
  N4: 부품1.GND, LED1.common_anode
