# Fritzing sketch AR14_sound (saved by Fritzing 0.9.3b)
breadboards: 1

parts:
  부품1 = Real Time Clock Breakout - DS1307 [part_number=147824]
  부품3 = Arduino Uno (Rev3)
  S4 = Pushbutton [package="[THT]"]
  S5 = Pushbutton [package="[THT]"]
  S6 = Pushbutton [package="[THT]"]
  LCD2 = LCD screen
  LED5 = Super Flux RGB LED (com. cathode)
  LED6 = Super Flux RGB LED (com. cathode)
  부품4 = Breakout Board for Electret Microphone

nets:
  GND: 부품1.GND, 부품3.GND, S4.Pin_3, S4.Pin_4, S5.Pin_3, S5.Pin_4, S6.Pin_3, S6.Pin_4, LCD2.VSS, LED5.green_anode, LED6.green_anode, 부품4.GND
  VCC: 부품1.VCC, 부품3.5V, LCD2.VDD, 부품4.VCC
  N1: 부품1.SDA, 부품3.D4
  N2: 부품1.SCL, 부품3.D3_PWM
  N3: 부품1.DS, 부품3.D2
  N4: 부품3.A0, 부품4.AUD
  N5: 부품3.A4/SDA, LCD2.V0
  N6: 부품3.A5/SCL, LCD2.RS
  N7: 부품3.D8, LED5.common_cathode, LED6.common_cathode
  N8: 부품3.D9_PWM, LED5.red_anode, LED6.red_anode
  N9: 부품3.D10_PWM/SS, LED5.blue_anode, LED6.blue_anode
  N10: 부품3.D1/TX, S6.Pin_1, S6.Pin_2
  N11: 부품3.D5_PWM, S4.Pin_1, S4.Pin_2
  N12: 부품3.D7, S5.Pin_1, S5.Pin_2

custom parts:
  Real Time Clock Breakout - DS1307: Two wire I2C interface; Hour : Minutes : Seconds AM/PM Day Month, Date - Year; Leap year compensation; Accurate calendar up to year 2100; DS1307 based RTC with LIR2032 battery (Battery include); 56 Bytes of Non-volatile memory available to user; Working time: 1 year
